# Fritzing sketch Schematic (saved by Fritzing 0.9.3b)
breadboards: 1

parts:
  TRS1 = Audio Jack (TRS) 3.5mm [package="4Ucon 08780 [THT]"]
  S1 = Pushbutton [package="[THT]"]
  S2 = Pushbutton [package="[THT]"]
  S3 = Pushbutton [package="[THT]"]
  S4 = Pushbutton [package="[THT]"]
  R1 = Resistor [tolerance=±5% resistance=220 package=THT]
  R2 = Resistor [tolerance=±5% resistance=220 package=THT]
  R3 = Resistor [tolerance=±5% resistance=220 package=THT]
  R4 = Resistor [tolerance=±5% resistance=220 package=THT]
  R5 = Resistor [tolerance=±5% resistance=220 package=THT]
  R6 = Resistor [tolerance=±5% resistance=220 package=THT]
  R7 = Resistor [tolerance=±5% resistance=220 package=THT]
  R8 = Resistor [tolerance=±5% resistance=220 package=THT]

nets:
  N1: TRS1.Tip, R5.Pin_1, R6.Pin_1, R7.Pin_1, R8.Pin_1
  N2: S1.Pin_1, S1.Pin_2
  N3: S1.Pin_3, S1.Pin_4
  N4: S2.Pin_1, S2.Pin_2, R4.Pin_1
  N5: S2.Pin_3, S2.Pin_4
  N6: S3.Pin_1, S3.Pin_2, R3.Pin_1
  N7: S3.Pin_3, S3.Pin_4
  N8: S4.Pin_1, S4.Pin_2, R2.Pin_1
  N9: S4.Pin_3, S4.Pin_4
  N10: R1.Pin_0, R2.Pin_0, R3.Pin_0, R4.Pin_0

notes:
  TI Tiva C Launchpad EK-TM4C123GXL.
  Input:
  switches 0-3 connected to PE0-3 (yellow), 4 resistors are 10k ohms.
  Output:
  4 resistors on right size (blue) are binary weighted DAC. The resistance in order for PB0-3: 12k, 6k, 3k,1.5k.
